// Logisim project alu.circ as structural Verilog: 1 circuit, main circuit alu
module alu (
  input  [31:0] A,
  input  [31:0] B,
  input  [3:0] ALUSel,
  output [31:0] Result
);

  wire comparator_1_lt;
  wire [31:0] add, and1, divider_1_out, divu, mulh, mulhu1, mult1, multiplier_3_out, multiplier_4_cout,
       multiplier_6_cout, nn, np, or1, pn, pp, remu, sll1, slt, sra1, srl1, sub, subtractor_2_out,
       subtractor_3_out, subtractor_5_out, subtractor_6_out, subtractor_7_out, subtractor_9_out, xor1;

  assign xor1 = A ^ B;  // XOR_Gate xor_1, 32 bits wide
  assign or1 = A | B;  // OR_Gate or_1, 32 bits wide
  Shifter #(.width(32), .shift("lr")) shifter_1 (.in(A), .\dist (B[4:0]), .out(srl1));
  Shifter #(.width(32)) shifter_2 (.in(A), .\dist (B[4:0]), .out(sll1));
  Adder #(.width(32)) adder_1 (.a(A), .b(B), .out(add));  // open: cin, cout
  Subtractor #(.width(32)) subtractor_1 (.a(A), .b(B), .out(sub));  // open: bin, bout
  Subtractor #(.width(32)) subtractor_2 (.a({32{1'b0}}), .b(A), .out(subtractor_2_out));  // open: bin, bout
  Subtractor #(.width(32)) subtractor_3 (.a({32{1'b0}}), .b(B), .out(subtractor_3_out));  // open: bin, bout
  Shifter #(.width(32), .shift("ar")) shifter_3 (.in(A), .\dist (B[4:0]), .out(sra1));
  Divider #(.width(32)) divider_1 (.a(A), .b(B), .out(divider_1_out));  // open: upper, rem
  Multiplier #(.width(32)) multiplier_1 (.a(A), .b(B), .cout(pp));  // open: out, cin
  Multiplier #(.width(32)) multiplier_2 (.a(subtractor_2_out), .b(subtractor_3_out), .cout(nn));  // open: out, cin
  assign and1 = A & B;  // AND_Gate and_1, 32 bits wide
  Multiplier #(.width(32)) multiplier_3 (.a(divider_1_out), .b(B), .out(multiplier_3_out));  // open: cin, cout
  Comparator #(.width(32)) comparator_1 (.a(A), .b(B), .lt(comparator_1_lt));  // open: gt, eq
  Subtractor #(.width(32)) subtractor_4 (.a(A), .b(multiplier_3_out), .out(remu));  // open: bin, bout
  Multiplexer #(.select(4), .width(32), .enable("false")) multiplexer_1 (
    .in0(add), .in1(and1), .in2(or1), .in3(xor1), .in4(srl1), .in5(sra1), .in6(sll1), .in7(slt), .in8(divu),
    .in9(remu), .in10(mult1), .in11(mulhu1), .in12(sub), .in13(B), .in14(mulh), .out(Result), .sel(ALUSel));  // open: in15
  assign slt = {{31{1'b0}}, comparator_1_lt};  // Bit_Extender bit_extender_1
  Divider #(.width(32)) divider_2 (.a(A), .b(B), .out(divu));  // open: upper, rem
  Subtractor #(.width(32)) subtractor_5 (.a({32{1'b0}}), .b(B), .out(subtractor_5_out));  // open: bin, bout
  Multiplier #(.width(32)) multiplier_4 (.a(A), .b(subtractor_5_out), .cout(multiplier_4_cout));  // open: out, cin
  Multiplier #(.width(32)) multiplier_5 (.a(A), .b(B), .out(mult1), .cout(mulhu1));  // open: cin
  Subtractor #(.width(32)) subtractor_6 (
    .a({32{1'b0}}), .b(multiplier_4_cout), .out(subtractor_6_out));  // open: bin, bout
  Subtractor #(.width(32)) subtractor_7 (.a({32{1'b0}}), .b(A), .out(subtractor_7_out));  // open: bin, bout
  Multiplexer #(.select(2), .width(32), .enable("false")) multiplexer_2 (
    .in0(pp), .in1(np), .in2(pn), .in3(nn), .out(mulh), .sel({B[31], A[31]}));
  Multiplier #(.width(32)) multiplier_6 (.a(B), .b(subtractor_7_out), .cout(multiplier_6_cout));  // open: out, cin
  Subtractor #(.width(32)) subtractor_8 (.a(subtractor_6_out), .b(32'h1), .out(pn));  // open: bin, bout
  Subtractor #(.width(32)) subtractor_9 (
    .a({32{1'b0}}), .b(multiplier_6_cout), .out(subtractor_9_out));  // open: bin, bout
  Subtractor #(.width(32)) subtractor_10 (.a(subtractor_9_out), .b(32'h1), .out(np));  // open: bin, bout

  // Other names for the same wires on the sheet: sign[1:0] = {B[31], A[31]}

  // Notes on the sheet:
  //   INPUTS to your circuit
  //   DON'T CHANGE THE LOCATIONS OF THE INPUTS AND OUTPUTS!
  //   OUTPUT from your circuit
endmodule
