// Logisim project regfile.circ as structural Verilog: 1 circuit, main circuit main
module main (
  input  [4:0] rs1,
  input  [4:0] rs2,
  input  [4:0] rd,
  input  [31:0] Write_Data,
  input  RegWEn,
  input  clk,
  output [31:0] ra,
  output [31:0] sp,
  output [31:0] t0,
  output [31:0] t1,
  output [31:0] t2,
  output [31:0] s0,
  output [31:0] s1,
  output [31:0] a0,
  output [31:0] Read_Data_1,
  output [31:0] Read_Data_2
);

  wire x0e, x1e, x2e, x5e, x6e, x7e, x8e, x9e, x10e;
  wire [31:0] x0input, x1input, x2input, x5input, x6input, x7input, x8input, x9input, x10input, zero;

  Multiplexer #(.select(5), .width(32), .enable("false")) multiplexer_1 (
    .in0(zero), .in1(ra), .in2(sp), .in5(t0), .in6(t1), .in7(t2), .in8(s0), .in9(s1), .in10(a0),
    .out(Read_Data_1), .sel(rs1));  // open: in3, in4, in11, in12, in13, in14, in15, in16, in17, in18, in19, in20, in21, in22, in23, in24, in25, in26, in27, in28, in29, in30, in31
  Register #(.width(32)) register_1 (.D(x6input), .en(x6e), .clk(clk), .Q(t1));  // open: clr
  Register #(.width(32)) x0 (.D({32{1'b0}}), .en(1'b0), .clk(clk), .Q(zero));  // open: clr
  Register #(.width(32)) register_2 (.D(x1input), .en(x1e), .clk(clk), .Q(ra));  // open: clr
  Register #(.width(32)) register_3 (.D(x2input), .en(x2e), .clk(clk), .Q(sp));  // open: clr
  Register #(.width(32)) register_4 (.D(x5input), .en(x5e), .clk(clk), .Q(t0));  // open: clr
  Multiplexer #(.select(5), .width(32), .enable("false")) multiplexer_2 (
    .in0(zero), .in1(ra), .in2(sp), .in5(t0), .in6(t1), .in7(t2), .in8(s0), .in9(s1), .in10(a0),
    .out(Read_Data_2), .sel(rs2));  // open: in3, in4, in11, in12, in13, in14, in15, in16, in17, in18, in19, in20, in21, in22, in23, in24, in25, in26, in27, in28, in29, in30, in31
  Register #(.width(32)) register_5 (.D(x8input), .en(x8e), .clk(clk), .Q(s0));  // open: clr
  Register #(.width(32)) register_6 (.D(x9input), .en(x9e), .clk(clk), .Q(s1));  // open: clr
  Register #(.width(32)) register_7 (.D(x10input), .en(x10e), .clk(clk), .Q(a0));  // open: clr
  Register #(.width(32)) register_8 (.D(x7input), .en(x7e), .clk(clk), .Q(t2));  // open: clr
  Demultiplexer #(.select(5), .width(32), .enable("false")) demultiplexer_1 (
    .out0(x0input), .out1(x1input), .out2(x2input), .out5(x5input), .out6(x6input), .out7(x7input),
    .out8(x8input), .out9(x9input), .out10(x10input), .in(Write_Data), .sel(rd));  // open: out3, out4, out11, out12, out13, out14, out15, out16, out17, out18, out19, out20, out21, out22, out23, out24, out25, out26, out27, out28, out29, out30, out31
  Demultiplexer #(.select(5), .enable("false")) demultiplexer_2 (
    .out0(x0e), .out1(x1e), .out2(x2e), .out5(x5e), .out6(x6e), .out7(x7e), .out8(x8e), .out9(x9e),
    .out10(x10e), .in(RegWEn), .sel(rd));  // open: out3, out4, out11, out12, out13, out14, out15, out16, out17, out18, out19, out20, out21, out22, out23, out24, out25, out26, out27, out28, out29, out30, out31

  // Other names for the same wires on the sheet: read_data1[31:0] = Read_Data_1; read_data2[31:0] = Read_Data_2;
  //   read_reg1[4:0] = rs1; read_reg2[4:0] = rs2; write_en = RegWEn; write_reg[4:0] = rd

  // Notes on the sheet:
  //   INPUTS to your circuit
  //   DON'T CHANGE THE LOCATIONS OF THE INPUTS AND OUTPUTS!
  //   These are DEBUG/TEST outputs from your circuit.
  //   OUTPUTS from your circuit
endmodule
